# Fritzing sketch Untitled Sketch 2 (saved by Fritzing 0.9.3b)

parts:
  Часть2 = Arduino Nano (Rev3.0) (ICSP)
  S3 = Toggle Switch [package=THT]
  GSM_SIM_GPSR_SMS_SIM900_SIM1 = SIM800L [package=THT]
  18650_holder1 = 18650 holder [package="DIP (Dual Inline) [THT]"]
  18650_holder2 = 18650 holder [package="DIP (Dual Inline) [THT]"]
  M1 = RioRand LM2596
  J1 = Piezo Speaker  # not connected
  R3 = Resistor [tolerance=±5% resistance=10k package="0603 [SMD]"]
  R5 = Resistor [tolerance=±5% resistance=10k package="0603 [SMD]"]

nets:
  N1: Часть2.GND, S3.L2, R3.Pin_1
  N2: Часть2.D10, R5.Pin_1
  N3: Часть2.D12/MISO, GSM_SIM_GPSR_SMS_SIM900_SIM1.SIM_TXD
  N4: Часть2.VIN, 18650_holder1.holder_+
  N5: S3.L1, 18650_holder2.holder_-
  N6: GSM_SIM_GPSR_SMS_SIM900_SIM1.5V, M1.Pin_3
  N7: GSM_SIM_GPSR_SMS_SIM900_SIM1.GND, M1.Pin_4
  N8: GSM_SIM_GPSR_SMS_SIM900_SIM1.SIM_RXD, R3.Pin_0, R5.Pin_0
  N9: 18650_holder1.holder_-, 18650_holder2.holder_+

custom parts:
  18650 holder: Акум формата 18650 в холдере
